// Logisim project SynthBite16.circ as structural Verilog: 1 circuit, main circuit SynthBite16
module SynthBite16 (
  input  in_1,
  input  in_2,
  input  in_3,
  input  [15:0] in_4,
  input  [15:0] in_5,
  input  in_6,
  input  in_7,
  input  in_8
);

  wire AC_p2, AC_p3, AC_p18, AC_p19, AC_p20, AC_p21, AC_p22, AC_p23, AC_p24, AC_p25, AC_p26, AC_p27, AC_p28,
       AC_p29, adder_1_cout, adder_2_cout, and_4_out, and_5_out, button_1_out, carry_q, comparator_1_eq,
       comparator_1_gt, comparator_1_lt, controlled_buffer_1_out, controlled_buffer_2_out,
       controlled_buffer_3_out, controlled_buffer_4_out, controlled_buffer_5_out, controlled_buffer_6_out,
       controlled_buffer_7_out, controlled_buffer_8_out, controlled_buffer_9_out, controlled_buffer_10_out,
       controlled_buffer_11_out, controlled_buffer_12_out, controlled_buffer_13_out,
       controlled_buffer_14_out, controlled_buffer_15_out, controlled_buffer_16_out, decoder_1_out0,
       decoder_1_out1, decoder_1_out2, decoder_1_out3, decoder_1_out4, decoder_2_out0, decoder_2_out1,
       decoder_2_out3, decoder_2_out10, decoder_2_out11, decoder_2_out12, decoder_2_out13, MasterClock_out,
       multiplexer_2_out, nand_1_out, not_2_out, or_2_out, or_3_out, or_5_out, shift_register_1_p1,
       subtractor_1_bout, undriven, undriven_2, undriven_5, undriven_6, undriven_7;
  wire [0:0] DR_q;
  wire [3:0] CWR_q;
  wire [7:0] register_10_q;
  wire [11:0] counter_1_q;
  wire [15:0] adder_1_out, adder_2_out, adder_3_out, and_1_out, and_2_out, and_3_out,
       controlled_buffer_17_out, DR_q_2, IR_q, mAC_p1, multiplexer_1_out, not_1_out, or_1_out, rand_q,
       register_9_q, subtractor_1_out, undriven_4, xor_1_out, xor_2_out;
  wire [15:15] undriven_3;
  wire [31:0] CNTRL_MEM_data, CWR_q_2;

  Controlled_Buffer controlled_buffer_1 (.out(controlled_buffer_1_out), .en(undriven));  // open: in
  Controlled_Buffer controlled_buffer_2 (.out(controlled_buffer_2_out), .en(undriven));  // open: in
  Controlled_Buffer controlled_buffer_3 (.out(controlled_buffer_3_out), .en(undriven));  // open: in
  Controlled_Buffer controlled_buffer_4 (.out(controlled_buffer_4_out), .en(undriven));  // open: in
  Controlled_Buffer controlled_buffer_5 (.out(controlled_buffer_5_out), .en(undriven));  // open: in
  Controlled_Buffer controlled_buffer_6 (.out(controlled_buffer_6_out), .en(undriven));  // open: in
  Controlled_Buffer controlled_buffer_7 (.out(controlled_buffer_7_out), .en(undriven));  // open: in
  Controlled_Buffer controlled_buffer_8 (.out(controlled_buffer_8_out), .en(undriven));  // open: in
  Controlled_Buffer controlled_buffer_9 (.out(controlled_buffer_9_out), .en(undriven));  // open: in
  Controlled_Buffer controlled_buffer_10 (.out(controlled_buffer_10_out), .en(undriven));  // open: in
  Controlled_Buffer controlled_buffer_11 (.out(controlled_buffer_11_out), .en(undriven));  // open: in
  Controlled_Buffer controlled_buffer_12 (.out(controlled_buffer_12_out), .en(undriven));  // open: in
  Controlled_Buffer controlled_buffer_13 (.out(controlled_buffer_13_out), .en(undriven));  // open: in
  Controlled_Buffer controlled_buffer_14 (.out(controlled_buffer_14_out), .en(undriven));  // open: in
  Controlled_Buffer controlled_buffer_15 (.out(controlled_buffer_15_out), .en(undriven));  // open: in
  Controlled_Buffer controlled_buffer_16 (.out(controlled_buffer_16_out), .en(undriven));  // open: in
  Clock MasterClock (.out(MasterClock_out));
  LED led_1 (.in(MasterClock_out));
  assign {{4{controlled_buffer_17_out[15]}}, controlled_buffer_17_out[11:0]} = decoder_1_out4 ? {{4{in_1}}, IR_q[15:4]} : 16'bz;  // Controlled_Buffer controlled_buffer_17
  Counter #(.max('h7), .width(3)) SR (.clr(button_1_out));  // open: load, up, count, clk, D, carry, Q
  LedBar #(.matrixcols(4)) ledbar_1 (
    .led0(controlled_buffer_17_out[15]), .led1(controlled_buffer_17_out[15]),
    .led2(controlled_buffer_17_out[15]), .led3(controlled_buffer_17_out[15]));
  Controlled_Buffer #(.width(16)) controlled_buffer_18 ();  // open: in, out, en
  Register #(.width(16)) DR (
    .D({{4{controlled_buffer_17_out[15]}}, controlled_buffer_17_out[11:0]}), .en(decoder_2_out10),
    .clk(MasterClock_out), .Q({DR_q_2[14:0], DR_q[0]}), .clr(button_1_out));
  Counter #(.max('hfff), .width(12)) counter_1 (
    .clr(button_1_out), .load(decoder_2_out3), .clk(MasterClock_out), .D(controlled_buffer_17_out[11:0]),
    .Q(counter_1_q));  // open: up, count, carry
  Register #(.width(16)) register_1 ();  // open: D, en, clk, Q, clr
  Register #(.width(16)) register_2 ();  // open: D, en, clk, Q, clr
  Register #(.width(16)) register_3 ();  // open: D, en, clk, Q, clr
  Register #(.width(16)) register_4 (.clr(undriven_2));  // open: D, en, clk, Q
  DotMatrix #(.matrixcols(16), .matrixrows(1)) dotmatrix_1 (
    .col0(controlled_buffer_17_out[15]), .col1(controlled_buffer_17_out[15]),
    .col2(controlled_buffer_17_out[15]), .col3(controlled_buffer_17_out[15]),
    .col4(controlled_buffer_17_out[11]), .col5(controlled_buffer_17_out[10]),
    .col6(controlled_buffer_17_out[9]), .col7(controlled_buffer_17_out[8]),
    .col8(controlled_buffer_17_out[7]), .col9(controlled_buffer_17_out[6]),
    .col10(controlled_buffer_17_out[5]), .col11(controlled_buffer_17_out[4]),
    .col12(controlled_buffer_17_out[3]), .col13(controlled_buffer_17_out[2]),
    .col14(controlled_buffer_17_out[1]), .col15(controlled_buffer_17_out[0]));
  Register #(.width(16)) register_5 ();  // open: D, en, clk, Q, clr
  Register #(.width(16)) register_6 ();  // open: D, en, clk, Q, clr
  Register #(.width(16)) register_7 ();  // open: D, en, clk, Q, clr
  Register #(.width(16)) register_8 ();  // open: D, en, clk, Q, clr
  assign controlled_buffer_17_out[0] = decoder_1_out3 ? counter_1_q[0] : 1'bz;  // Controlled_Buffer controlled_buffer_19
  assign controlled_buffer_17_out[1] = decoder_1_out3 ? counter_1_q[1] : 1'bz;  // Controlled_Buffer controlled_buffer_20
  assign controlled_buffer_17_out[2] = decoder_1_out3 ? counter_1_q[2] : 1'bz;  // Controlled_Buffer controlled_buffer_21
  assign controlled_buffer_17_out[3] = decoder_1_out3 ? counter_1_q[3] : 1'bz;  // Controlled_Buffer controlled_buffer_22
  assign controlled_buffer_17_out[4] = decoder_1_out3 ? counter_1_q[4] : 1'bz;  // Controlled_Buffer controlled_buffer_23
  assign controlled_buffer_17_out[5] = decoder_1_out3 ? counter_1_q[5] : 1'bz;  // Controlled_Buffer controlled_buffer_24
  assign controlled_buffer_17_out[6] = decoder_1_out3 ? counter_1_q[6] : 1'bz;  // Controlled_Buffer controlled_buffer_25
  assign controlled_buffer_17_out[7] = decoder_1_out3 ? counter_1_q[7] : 1'bz;  // Controlled_Buffer controlled_buffer_26
  assign controlled_buffer_17_out[8] = decoder_1_out3 ? counter_1_q[8] : 1'bz;  // Controlled_Buffer controlled_buffer_27
  assign controlled_buffer_17_out[9] = decoder_1_out3 ? counter_1_q[9] : 1'bz;  // Controlled_Buffer controlled_buffer_28
  assign controlled_buffer_17_out[10] = decoder_1_out3 ? counter_1_q[10] : 1'bz;  // Controlled_Buffer controlled_buffer_29
  assign controlled_buffer_17_out[11] = decoder_1_out3 ? counter_1_q[11] : 1'bz;  // Controlled_Buffer controlled_buffer_30
  assign controlled_buffer_17_out[15] = decoder_1_out3 ? in_7 : 1'bz;  // Controlled_Buffer controlled_buffer_31
  Register #(.width(16)) IR (
    .D({{4{controlled_buffer_17_out[15]}}, controlled_buffer_17_out[11:0]}), .en(decoder_2_out11),
    .clk(MasterClock_out), .Q(IR_q), .clr(button_1_out));
  Button button_1 (.out(button_1_out));
  LedBar #(.matrixcols(4)) ledbar_2 (.led0(IR_q[0]), .led1(IR_q[1]), .led2(IR_q[2]), .led3(IR_q[3]));
  Adder #(.width(16)) adder_1 (
    .a({DR_q_2[14:0], DR_q[0]}), .b({{4{controlled_buffer_17_out[15]}}, controlled_buffer_17_out[11:0]}),
    .out(adder_1_out), .cin(DR_q_2[15]), .cout(adder_1_cout));
  assign and_1_out = rand_q & {{4{controlled_buffer_17_out[15]}}, controlled_buffer_17_out[11:0]};  // AND_Gate and_1, 16 bits wide
  Subtractor #(.width(16)) subtractor_1 (
    .a({DR_q_2[14:0], DR_q[0]}), .b({{4{controlled_buffer_17_out[15]}}, controlled_buffer_17_out[11:0]}),
    .out(subtractor_1_out), .bin(DR_q_2[15]), .bout(subtractor_1_bout));
  assign or_1_out = {{4{controlled_buffer_17_out[15]}}, controlled_buffer_17_out[11:0]} | {DR_q_2[14:0], DR_q[0]};  // OR_Gate or_1, 16 bits wide
  assign xor_1_out = rand_q ^ and_1_out;  // XOR_Gate xor_1, 16 bits wide
  or or_2 (or_2_out, adder_1_cout, subtractor_1_bout);
  assign xor_2_out = {{4{controlled_buffer_17_out[15]}}, controlled_buffer_17_out[11:0]} ^ {DR_q_2[14:0], DR_q[0]};  // XOR_Gate xor_2, 16 bits wide
  Register #(.width(16)) \rand  (.D(xor_1_out), .en(in_8), .clk(MasterClock_out), .Q(rand_q));  // open: clr
  or or_3 (or_3_out, DR_q[0], adder_2_cout);
  or or_4 (CWR_q_2[18], or_2_out, or_3_out);
  assign and_2_out = {DR_q_2[14:0], DR_q[0]} & {16{undriven_3[15]}};  // AND_Gate and_2, 16 bits wide
  Adder #(.width(16)) adder_2 (.a(mAC_p1), .b(and_2_out), .out(adder_2_out), .cin(in_6), .cout(adder_2_cout));
  assign and_3_out = {{4{controlled_buffer_17_out[15]}}, controlled_buffer_17_out[11:0]} & {DR_q_2[14:0], DR_q[0]};  // AND_Gate and_3, 16 bits wide
  // Shift_Register #(.length(16)) mAC: pin names not known; wires that end beside it: mAC_p1, CWR_q_2[19], CWR_q_2[14], CWR_q_2[15], MasterClock_out, in_6, mAC_p1[0], mAC_p1[1], mAC_p1[2], mAC_p1[3], mAC_p1[4], mAC_p1[5], mAC_p1[6], mAC_p1[7], mAC_p1[8], mAC_p1[9], mAC_p1[10], mAC_p1[11]
  Register #(.width(16)) register_9 (
    .D({{4{controlled_buffer_17_out[15]}}, controlled_buffer_17_out[11:0]}), .en(decoder_2_out12),
    .clk(MasterClock_out), .Q(register_9_q), .clr(button_1_out));
  Adder #(.width(16)) adder_3 (
    .a(in_5), .b({{4{controlled_buffer_17_out[15]}}, controlled_buffer_17_out[11:0]}), .out(adder_3_out));  // open: cin, cout
  Comparator #(.width(16)) comparator_1 (
    .a({{4{controlled_buffer_17_out[15]}}, controlled_buffer_17_out[11:0]}), .b({DR_q_2[14:0], DR_q[0]}),
    .gt(comparator_1_gt), .eq(comparator_1_eq), .lt(comparator_1_lt));
  Hex_Digit_Display #(.decimalPoint("false")) hex_digit_display_1 (.value(register_9_q[15:12]));
  Hex_Digit_Display #(.decimalPoint("false")) hex_digit_display_2 (.value(register_9_q[11:8]));
  Hex_Digit_Display #(.decimalPoint("false")) hex_digit_display_3 (.value(register_9_q[7:4]));
  Hex_Digit_Display #(.decimalPoint("false")) hex_digit_display_4 (.value(register_9_q[3:0]));
  Register register_10 (.D({8{in_2}}), .en(in_3), .clk(MasterClock_out), .Q(register_10_q), .clr(button_1_out));
  assign not_1_out = ~{DR_q_2[14:0], DR_q[0]};  // NOT_Gate not_1, 16 bits wide
  // Shift_Register #(.length(16)) shift_register_1: pin names not known; wires that end beside it: shift_register_1_p1
  ROM #(.dataWidth(32)) CNTRL_MEM (.addr(register_10_q), .data(CNTRL_MEM_data));
  Register #(.trigger("falling"), .width(32)) CWR (
    .D(CNTRL_MEM_data), .en(1'b1), .clk(MasterClock_out), .Q({CWR_q_2[31:12], CWR_q, CWR_q_2[7:0]}),
    .clr(button_1_out));
  Multiplexer #(.enable("true"), .select(4), .width(16)) multiplexer_1 (
    .in0({DR_q_2[14:0], DR_q[0]}), .in1(not_1_out), .in2(adder_1_out), .in3(subtractor_1_out),
    .in4(or_1_out), .in5(xor_2_out), .in6(and_3_out), .in7(DR_q_2), .in8(in_4), .in9(rand_q),
    .in10(adder_3_out), .in11(mAC_p1), .in12(undriven_4), .in13(in_4), .in14(in_4), .in15(in_4),
    .out(multiplexer_1_out), .sel(CWR_q), .en(CWR_q_2[12]));
  DotMatrix #(.matrixcols(32), .matrixrows(1)) dotmatrix_2 (
    .col0(CWR_q_2[0]), .col1(CWR_q_2[1]), .col2(CWR_q_2[2]), .col3(CWR_q_2[3]), .col4(CWR_q_2[4]),
    .col5(CWR_q_2[5]), .col6(CWR_q_2[6]), .col7(CWR_q_2[7]), .col8(CWR_q[0]), .col9(CWR_q[1]),
    .col10(CWR_q[2]), .col11(CWR_q[3]), .col12(CWR_q_2[12]), .col13(CWR_q_2[13]), .col14(CWR_q_2[14]),
    .col15(CWR_q_2[15]), .col16(CWR_q_2[16]), .col17(CWR_q_2[17]), .col18(CWR_q_2[18]), .col19(CWR_q_2[19]),
    .col20(CWR_q_2[20]), .col21(CWR_q_2[21]), .col22(CWR_q_2[22]), .col23(CWR_q_2[23]), .col24(CWR_q_2[24]),
    .col25(CWR_q_2[25]), .col26(CWR_q_2[26]), .col27(CWR_q_2[27]), .col28(CWR_q_2[28]), .col29(CWR_q_2[29]),
    .col30(CWR_q_2[30]), .col31(CWR_q_2[31]));
  nand nand_1 (nand_1_out, CWR_q[1], CWR_q[0]);
  not not_2 (not_2_out, CWR_q[2]);
  and and_4 (and_4_out, not_2_out, nand_1_out);
  and and_5 (and_5_out, CWR_q[3], and_4_out);
  Multiplexer #(.select(2)) multiplexer_2 (
    .in0(carry_q), .in1(comparator_1_lt), .in2(comparator_1_eq), .in3(comparator_1_gt),
    .out(multiplexer_2_out), .sel(CWR_q_2[17:16]));
  // Shift_Register #(.length(16)) AC: pin names not known; wires that end beside it: button_1_out, AC_p2, AC_p3, MasterClock_out, DR_q_2[15], multiplexer_1_out[0], multiplexer_1_out[1], multiplexer_1_out[2], multiplexer_1_out[3], multiplexer_1_out[4], multiplexer_1_out[5], multiplexer_1_out[6], multiplexer_1_out[7], multiplexer_1_out[8], multiplexer_1_out[9], multiplexer_1_out[10], multiplexer_1_out[11], AC_p18, AC_p19, AC_p20, AC_p21, AC_p22, AC_p23, AC_p24, AC_p25, AC_p26, AC_p27, AC_p28, AC_p29
  RAM #(.addrWidth(12), .asyncread("true"), .dataWidth(16), .databus("bidir")) MEM (
    .addr(counter_1_q), .we(decoder_2_out1), .oe(decoder_1_out1), .clk(MasterClock_out),
    .data({{4{controlled_buffer_17_out[15]}}, controlled_buffer_17_out[11:0]}));
  Decoder #(.enable("false"), .select(4)) decoder_1 (
    .out0(decoder_1_out0), .out1(decoder_1_out1), .out2(decoder_1_out2), .out3(decoder_1_out3),
    .out4(decoder_1_out4), .out10(shift_register_1_p1), .sel(CWR_q_2[3:0]));  // open: out5, out6, out7, out8, out9, out11, out12, out13, out14, out15
  Decoder #(.enable("false"), .select(4)) decoder_2 (
    .out0(decoder_2_out0), .out1(decoder_2_out1), .out2(AC_p2), .out3(decoder_2_out3),
    .out10(decoder_2_out10), .out11(decoder_2_out11), .out12(decoder_2_out12), .out13(decoder_2_out13),
    .sel(CWR_q_2[7:4]));  // open: out4, out5, out6, out7, out8, out9, out14, out15
  D_Flip_Flop carry (.D(CWR_q_2[18]), .clk(MasterClock_out), .Q(carry_q), .reset(button_1_out));  // open: Qn, preset
  or or_5 (or_5_out, CWR_q_2[18], multiplexer_2_out);
  assign controlled_buffer_17_out[0] = decoder_1_out2 ? AC_p18 : 1'bz;  // Controlled_Buffer controlled_buffer_32
  assign controlled_buffer_17_out[1] = decoder_1_out2 ? AC_p19 : 1'bz;  // Controlled_Buffer controlled_buffer_33
  assign controlled_buffer_17_out[2] = decoder_1_out2 ? AC_p20 : 1'bz;  // Controlled_Buffer controlled_buffer_34
  assign controlled_buffer_17_out[3] = decoder_1_out2 ? AC_p21 : 1'bz;  // Controlled_Buffer controlled_buffer_35
  assign controlled_buffer_17_out[4] = decoder_1_out2 ? AC_p22 : 1'bz;  // Controlled_Buffer controlled_buffer_36
  assign controlled_buffer_17_out[5] = decoder_1_out2 ? AC_p23 : 1'bz;  // Controlled_Buffer controlled_buffer_37
  assign controlled_buffer_17_out[6] = decoder_1_out2 ? AC_p24 : 1'bz;  // Controlled_Buffer controlled_buffer_38
  assign controlled_buffer_17_out[7] = decoder_1_out2 ? AC_p25 : 1'bz;  // Controlled_Buffer controlled_buffer_39
  assign controlled_buffer_17_out[8] = decoder_1_out2 ? AC_p26 : 1'bz;  // Controlled_Buffer controlled_buffer_40
  assign controlled_buffer_17_out[9] = decoder_1_out2 ? AC_p27 : 1'bz;  // Controlled_Buffer controlled_buffer_41
  assign controlled_buffer_17_out[10] = decoder_1_out2 ? AC_p28 : 1'bz;  // Controlled_Buffer controlled_buffer_42
  assign controlled_buffer_17_out[11] = decoder_1_out2 ? AC_p29 : 1'bz;  // Controlled_Buffer controlled_buffer_43
  assign controlled_buffer_17_out[15] = decoder_1_out2 ? undriven_5 : 1'bz;  // Controlled_Buffer controlled_buffer_44
  assign controlled_buffer_17_out[15] = decoder_1_out2 ? undriven_6 : 1'bz;  // Controlled_Buffer controlled_buffer_45
  assign controlled_buffer_17_out[15] = decoder_1_out2 ? undriven_7 : 1'bz;  // Controlled_Buffer controlled_buffer_46
  assign controlled_buffer_17_out[15] = decoder_1_out2 ? undriven_3[15] : 1'bz;  // Controlled_Buffer controlled_buffer_47
  LED led_2 (.in(decoder_1_out0));
  LED led_3 (.in(decoder_2_out0));
  Register #(.width(1)) register_11 (.D(or_5_out), .clk(MasterClock_out));  // open: en, Q, clr
  D_Flip_Flop d_ff_1 (.D(decoder_2_out13), .clk(MasterClock_out), .Q(DR_q_2[15]));  // open: Qn, preset, reset
  or or_6 (AC_p3, and_5_out, CWR_q_2[13]);

  // Notes on the sheet:
  //   CLOCK
  //   SYSTEM BUS
  //   16 LINES
  //   PRESENT BUS VALUES
  //   COMPUTER ON
  //   NXT INSN FRM MEM OR CNTRL MEM
  //   AC RESET ASYNC
  //   ALU
  //   LEAST SIGNIFICANT LINE
  //   CONTROL UNIT
  //   MOST SIGNIFICANT LINE
  //   OUTPUT
  //   contents of CNTRL_MEM (hex, n*v repeats v):
  //   1111111
  //   this line is just a place holder
  //   PRESENT CONTROL
  //   ACC SHIFT(L)
  //   NONE
  //   MEM OUT ENABLE
  //   ACC ON BUS
  //   PC ON BUS
  //   PC ON BUS
  //   NONE
  //   AC PARLLEL LOAD
  //   PC LOAD
  //   DR LOAD
  //   IR LOAD
  //   OUT LOAD
  //   SRL IN
  //   CONDITION FLIP FLOP
  //   PUT ON BUS
  //   MEM WRITE ENABLE
  //   SERIAL IN
  //   LOAD FROM BUS
endmodule
